// Logisim project Guess_The_Number_Xtreme.circ as structural Verilog: 9 circuits, main circuit main
// x
module main (
  input  in_1,
  input  in_2,
  input  in_3,
  input  in_4,
  input  in_5,
  input  in_6,
  input  in_7,
  input  in_8
);

  wire A_JOGADO, A_VENCEU, ACERTOU, B_JOGADO, B_VENCEU, CHUTANDO_X, CHUTANDO_Y, chutar, CONFIGURAR, EMPATE,
       FIM_DE_JOGO, IGUAL, MAIOR, MENOR, proximo, RESET, START, tunnel;
  wire [3:0] GA, GB, XH, YH;

  Button button_1 ();  // open: out
  Button button_2 ();  // open: out
  Hex_Digit_Display hex_digit_display_1 ();  // open: value, dp
  Hex_Digit_Display hex_digit_display_2 ();  // open: value, dp
  LED led_1 ();  // open: in
  Hex_Digit_Display hex_digit_display_3 ();  // open: value, dp
  Button button_3 ();  // open: out
  LED #(.active("false")) led_2 ();  // open: in
  LED #(.active("false")) led_3 ();  // open: in
  Hex_Digit_Display hex_digit_display_4 ();  // open: value, dp
  Hex_Digit_Display hex_digit_display_5 (.value(GA));  // open: dp
  LED led_4 (.in(A_JOGADO));
  Button button_4 ();  // open: out
  Hex_Digit_Display hex_digit_display_6 ();  // open: value, dp
  LED led_5 ();  // open: in
  LED led_6 (.in(A_VENCEU));
  Button button_5 (.out(START));
  LED led_7 (.in(MAIOR));
  Button button_6 (.out(proximo));
  Hex_Digit_Display hex_digit_display_7 (.value(XH));  // open: dp
  LED led_8 (.in(CHUTANDO_X));
  LED led_9 (.in(FIM_DE_JOGO));
  LED led_10 (.in(EMPATE));
  LED led_11 (.in(tunnel));
  Button button_7 (.out(CONFIGURAR));
  LED led_12 (.in(ACERTOU));
  LED led_13 (.in(IGUAL));
  Button button_8 (.out(chutar));
  LED led_14 ();  // open: in
  Hex_Digit_Display hex_digit_display_8 (.value(YH));  // open: dp
  LED led_15 (.in(CHUTANDO_Y));
  LED led_16 (.in(B_VENCEU));
  Button button_9 (.out(RESET));
  LED led_17 (.in(MENOR));
  Hex_Digit_Display hex_digit_display_9 ();  // open: value, dp
  Hex_Digit_Display hex_digit_display_10 ();  // open: value, dp
  LED #(.active("false")) led_18 ();  // open: in
  LED #(.active("false")) led_19 ();  // open: in
  Hex_Digit_Display hex_digit_display_11 ();  // open: value, dp
  LED led_20 ();  // open: in
  Hex_Digit_Display hex_digit_display_12 (.value(GB));  // open: dp
  LED led_21 (.in(B_JOGADO));
  Hex_Digit_Display hex_digit_display_13 ();  // open: value, dp
  Hex_Digit_Display hex_digit_display_14 ();  // open: value, dp
  // Coordenadas coordenadas_1: pin names not known; wires that end beside it: proximo, chutar, 4'b1111, CHUTANDO_X, 4'b1111, CHUTANDO_Y, MAIOR, IGUAL, MENOR, XH, YH
  Entrada entrada_1 (.A3(in_1), .A2(in_2), .A1(in_3), .A0(in_4), .resultado(GA));
  Entrada entrada_2 (.A3(in_5), .A2(in_6), .A1(in_7), .A0(in_8), .resultado(GB));
  decrementar_min_sec decrementar_min_sec_1 ();  // open: Clear, Enable

  // Other names for the same wires on the sheet: A0 = in_4; A1 = in_3; A2 = in_2; A3 = in_1; B0 = in_8; B1 = in_7;
  //   B2 = in_6; B3 = in_5
endmodule

module Flip_Flop_SR (
  input  S_R,
  input  Clock,
  input  Preset,
  input  Enable,
  input  Clear,
  output out_6
);

  wire not_1_out;

  not not_1 (not_1_out, S_R);
  S_R_Flip_Flop s_r_ff_1 (
    .S(S_R), .clk(Clock), .R(not_1_out), .Q(out_6), .preset(Preset), .reset(Clear), .en(Enable));  // open: Qn
endmodule

module Decrementador (
  input  Clock,
  input  Preset,
  input  Enable,
  input  Clear,
  input  [3:0] valor_retorno,
  output [3:0] out_6
);

  wire comparator_1_eq;
  wire [3:0] adder_1_out, multiplexer_1_out;

  Hex_Digit_Display hex_digit_display_1 (.value(out_6));  // open: dp
  Flip_Flop_SR flip_flop_sr_1 (
    .S_R(multiplexer_1_out[3]), .Clock(Clock), .Preset(Preset), .Enable(Enable), .Clear(Clear),
    .out_6(out_6[3]));
  Flip_Flop_SR flip_flop_sr_2 (
    .S_R(multiplexer_1_out[2]), .Clock(Clock), .Preset(Preset), .Enable(Enable), .Clear(Clear),
    .out_6(out_6[2]));
  Flip_Flop_SR flip_flop_sr_3 (
    .S_R(multiplexer_1_out[1]), .Clock(Clock), .Preset(Preset), .Enable(Enable), .Clear(Clear),
    .out_6(out_6[1]));
  Multiplexer #(.width(4)) multiplexer_1 (
    .in0(adder_1_out), .in1(valor_retorno), .out(multiplexer_1_out), .sel(comparator_1_eq));  // open: en
  Flip_Flop_SR flip_flop_sr_4 (
    .S_R(multiplexer_1_out[0]), .Clock(Clock), .Preset(Preset), .Enable(Enable), .Clear(Clear),
    .out_6(out_6[0]));
  Hex_Digit_Display hex_digit_display_2 (.value(adder_1_out));  // open: dp
  Adder #(.width(4)) adder_1 (.a(out_6), .b(4'b1111), .out(adder_1_out));  // open: cin, cout
  Comparator #(.width(4)) comparator_1 (.a(adder_1_out), .b(4'b1111), .eq(comparator_1_eq));  // open: gt, lt
endmodule

module Verificador_9 (
  input  Enable
);

  wire and_1_out, clock_1_out, comparator_1_eq, comparator_2_eq, comparator_3_eq, comparator_4_eq, not_1_out;
  wire [3:0] and_2_out, decrementador_1_out_6, decrementador_2_out_6, decrementador_3_out_6,
       decrementador_4_out_6;

  and and_1 (and_1_out, Enable, not_1_out);
  not not_1 (not_1_out, comparator_2_eq);
  Hex_Digit_Display hex_digit_display_1 (.value(decrementador_1_out_6));  // open: dp
  Decrementador decrementador_1 (
    .Clock(comparator_1_eq), .Enable(and_1_out), .valor_retorno(4'b0101), .out_6(decrementador_1_out_6));  // open: Preset, Clear
  Hex_Digit_Display hex_digit_display_2 (.value(decrementador_2_out_6));  // open: dp
  Decrementador decrementador_2 (
    .Clock(comparator_3_eq), .Enable(and_1_out), .valor_retorno(4'b1001), .out_6(decrementador_2_out_6));  // open: Preset, Clear
  Comparator #(.width(4)) comparator_1 (.a(decrementador_2_out_6), .b(4'b1001), .eq(comparator_1_eq));  // open: gt, lt
  assign and_2_out = ~decrementador_1_out_6 & ~decrementador_2_out_6 & ~decrementador_3_out_6 & ~decrementador_4_out_6;  // AND_Gate and_2, 4 bits wide
  Hex_Digit_Display hex_digit_display_3 (.value(decrementador_3_out_6));  // open: dp
  Decrementador decrementador_3 (
    .Clock(comparator_4_eq), .Enable(and_1_out), .valor_retorno(4'b0101), .out_6(decrementador_3_out_6));  // open: Preset, Clear
  Comparator #(.width(4)) comparator_2 (.a(and_2_out), .b(4'b1111), .eq(comparator_2_eq));  // open: gt, lt
  Comparator #(.width(4)) comparator_3 (.a(decrementador_3_out_6), .b(4'b0101), .eq(comparator_3_eq));  // open: gt, lt
  Hex_Digit_Display hex_digit_display_4 (.value(decrementador_4_out_6));  // open: dp
  Decrementador decrementador_4 (
    .Clock(clock_1_out), .Enable(and_1_out), .valor_retorno(4'b1001), .out_6(decrementador_4_out_6));  // open: Preset, Clear
  Comparator #(.width(4)) comparator_4 (.a(decrementador_4_out_6), .b(4'b1001), .eq(comparator_4_eq));  // open: gt, lt
  Clock clock_1 (.out(clock_1_out));
endmodule

module decrementar_min_sec (
  input  Clear,
  input  Enable
);

  wire and_2_out, button_1_out, button_2_out, button_3_out, button_4_out, clock_1_out, comparator_1_eq,
       comparator_2_eq, comparator_3_eq, comparator_4_eq, multiplexer_1_out, multiplexer_2_out,
       multiplexer_3_out, multiplexer_4_out, not_1_out, not_2_out, or_1_out, or_2_out, or_3_out, or_4_out;
  wire [3:0] and_1_out, decrementador_1_out_6, decrementador_2_out_6, decrementador_3_out_6,
       decrementador_4_out_6;

  not not_1 (not_1_out, Enable);
  Hex_Digit_Display hex_digit_display_1 (.value(decrementador_1_out_6));  // open: dp
  Decrementador decrementador_1 (
    .Clock(multiplexer_1_out), .Enable(or_1_out), .Clear(Clear), .valor_retorno(4'b0101),
    .out_6(decrementador_1_out_6));  // open: Preset
  or or_1 (or_1_out, Enable, not_1_out);
  Multiplexer multiplexer_1 (
    .in0(button_1_out), .in1(comparator_1_eq), .out(multiplexer_1_out), .sel(Enable));  // open: en
  Button button_1 (.out(button_1_out));
  Hex_Digit_Display hex_digit_display_2 (.value(decrementador_2_out_6));  // open: dp
  Decrementador decrementador_2 (
    .Clock(multiplexer_2_out), .Enable(or_2_out), .Clear(Clear), .valor_retorno(4'b1001),
    .out_6(decrementador_2_out_6));  // open: Preset
  or or_2 (or_2_out, Enable, not_1_out);
  Multiplexer multiplexer_2 (
    .in0(button_2_out), .in1(comparator_2_eq), .out(multiplexer_2_out), .sel(Enable));  // open: en
  Button button_2 (.out(button_2_out));
  Comparator #(.width(4)) comparator_1 (.a(decrementador_2_out_6), .b(4'b1001), .eq(comparator_1_eq));  // open: gt, lt
  assign and_1_out = ~decrementador_1_out_6 & ~decrementador_2_out_6 & ~decrementador_3_out_6 & ~decrementador_4_out_6;  // AND_Gate and_1, 4 bits wide
  Hex_Digit_Display hex_digit_display_3 (.value(decrementador_3_out_6));  // open: dp
  Decrementador decrementador_3 (
    .Clock(multiplexer_3_out), .Enable(or_3_out), .Clear(Clear), .valor_retorno(4'b0101),
    .out_6(decrementador_3_out_6));  // open: Preset
  or or_3 (or_3_out, Enable, not_1_out);
  Multiplexer multiplexer_3 (
    .in0(button_3_out), .in1(comparator_4_eq), .out(multiplexer_3_out), .sel(Enable));  // open: en
  Button button_3 (.out(button_3_out));
  Comparator #(.width(4)) comparator_2 (.a(decrementador_3_out_6), .b(4'b0101), .eq(comparator_2_eq));  // open: gt, lt
  Comparator #(.width(4)) comparator_3 (.a(and_1_out), .b(4'b1111), .eq(comparator_3_eq));  // open: gt, lt
  Hex_Digit_Display hex_digit_display_4 (.value(decrementador_4_out_6));  // open: dp
  Decrementador decrementador_4 (
    .Clock(multiplexer_4_out), .Enable(or_4_out), .Clear(Clear), .valor_retorno(4'b1001),
    .out_6(decrementador_4_out_6));  // open: Preset
  or or_4 (or_4_out, Enable, not_1_out);
  Multiplexer multiplexer_4 (.in0(button_4_out), .in1(and_2_out), .out(multiplexer_4_out), .sel(Enable));  // open: en
  Button button_4 (.out(button_4_out));
  Comparator #(.width(4)) comparator_4 (.a(decrementador_4_out_6), .b(4'b1001), .eq(comparator_4_eq));  // open: gt, lt
  and and_2 (and_2_out, not_2_out, clock_1_out);
  Clock clock_1 (.out(clock_1_out));
  not not_2 (not_2_out, comparator_3_eq);
endmodule

module Entrada (
  input  A3,
  input  A2,
  input  A1,
  input  A0,
  output [3:0] resultado
);

  Hex_Digit_Display hex_digit_display_1 (.value({A3, A2, A1, A0}));  // open: dp

  assign resultado = {A3, A2, A1, A0};
endmodule

// coordenadas
module Coordenadas (
  input  [3:0] a,
  input  [3:0] b,
  input  proximo,
  input  chutar,
  output MAIOR,
  output IGUAL,
  output MENOR,
  output [3:0] saidax,
  output [3:0] saiday,
  output Chutando_Y,
  output Chutando_X
);

  wire and_1_out, and_2_out, comparator_1_eq, comparator_3_eq, comparator_4_eq, comparator_5_eq,
       comparator_8_eq, comparator_8_gt, comparator_8_lt;
  wire [3:0] adder_1_out, adder_2_out, flip_flop_condicao_1_valor_saida, flip_flop_condicao_2_valor_saida,
       multiplexer_1_out, multiplexer_2_out;

  Hex_Digit_Display hex_digit_display_1 (.value(flip_flop_condicao_1_valor_saida));  // open: dp
  flip_flop_condicao flip_flop_condicao_1 (
    .Clock(proximo), .Preset(1'b0), .Enable(1'b1), .Clear(1'b0), .valor_retorno(4'b0000),
    .valor_max__1(4'b0011), .valor_saida(flip_flop_condicao_1_valor_saida));
  Comparator #(.width(4)) comparator_1 (
    .a(flip_flop_condicao_1_valor_saida), .b(4'b0010), .eq(comparator_1_eq));  // open: gt, lt
  Comparator comparator_2 ();  // open: a, b, gt, eq, lt
  flip_flop_condicao flip_flop_condicao_2 (
    .Clock(comparator_1_eq), .Enable(1'b1), .Clear(1'b0), .valor_retorno(4'b0000), .valor_max__1(4'b0010),
    .valor_saida(flip_flop_condicao_2_valor_saida));  // open: Preset
  Comparator #(.width(4)) comparator_3 (
    .a(flip_flop_condicao_2_valor_saida), .b(4'b0000), .eq(comparator_3_eq));  // open: gt, lt
  Comparator #(.width(4)) comparator_4 (
    .a(flip_flop_condicao_1_valor_saida), .b(4'b0000), .eq(comparator_4_eq));  // open: gt, lt
  Comparator #(.width(4)) comparator_5 (
    .a(flip_flop_condicao_1_valor_saida), .b(4'b0001), .eq(comparator_5_eq));  // open: gt, lt
  Comparator #(.width(4)) comparator_6 (
    .a(flip_flop_condicao_1_valor_saida), .b(4'b0000), .eq(Chutando_X));  // open: gt, lt
  Multiplexer #(.width(4)) multiplexer_1 (
    .in0(a), .in1(b), .out(multiplexer_1_out), .sel(comparator_3_eq));  // open: en
  Register #(.width(4)) register_1 (.D(multiplexer_1_out), .Q(saidax), .clk(and_1_out));  // open: en, clr
  and and_1 (and_1_out, comparator_4_eq, chutar);
  Hex_Digit_Display hex_digit_display_2 (.value(saidax));  // open: dp
  LED u_Chutando_X (.in(Chutando_X));
  Multiplexer #(.width(4)) multiplexer_2 (
    .in0(a), .in1(b), .out(multiplexer_2_out), .sel(comparator_3_eq));  // open: en
  and and_2 (and_2_out, chutar, comparator_5_eq);
  Hex_Digit_Display hex_digit_display_3 (.value(saiday));  // open: dp
  Comparator #(.width(4)) comparator_7 (
    .a(flip_flop_condicao_1_valor_saida), .b(4'b0001), .eq(Chutando_Y));  // open: gt, lt
  Register #(.width(4)) register_2 (.D(multiplexer_2_out), .Q(saiday), .clk(and_2_out));  // open: en, clr
  LED u_Chutando_Y (.in(Chutando_Y));
  Hex_Digit_Display hex_digit_display_4 ();  // open: value, dp
  Adder #(.width(4)) adder_1 (.a(saidax), .b(saiday), .out(adder_1_out));  // open: cin, cout
  Adder #(.width(4)) adder_2 (.a(4'b0010), .b(4'b0010), .out(adder_2_out));  // open: cin, cout
  Comparator #(.width(4)) comparator_8 (
    .a(adder_1_out), .b(adder_2_out), .gt(comparator_8_gt), .eq(comparator_8_eq), .lt(comparator_8_lt));
  and and_3 (MAIOR, comparator_1_eq, comparator_8_gt);
  and and_4 (IGUAL, comparator_1_eq, comparator_8_eq);
  and and_5 (MENOR, comparator_1_eq, comparator_8_lt);
  LED A___B (.in(MAIOR));
  LED A____B (.in(IGUAL));
  LED A___B_2 (.in(MENOR));
endmodule

module flip_flop_condicao (
  input  Clock,
  input  Preset,
  input  Enable,
  input  Clear,
  input  [3:0] valor_retorno,
  input  [3:0] valor_max__1,
  output [3:0] valor_saida
);

  wire comparator_1_eq;
  wire [3:0] adder_1_out, multiplexer_1_out;

  Hex_Digit_Display hex_digit_display_1 (.value(valor_saida));  // open: dp
  Flip_Flop_SR flip_flop_sr_1 (
    .S_R(multiplexer_1_out[3]), .Clock(Clock), .Preset(Preset), .Enable(Enable), .Clear(Clear),
    .out_6(valor_saida[3]));
  Flip_Flop_SR flip_flop_sr_2 (
    .S_R(multiplexer_1_out[2]), .Clock(Clock), .Preset(Preset), .Enable(Enable), .Clear(Clear),
    .out_6(valor_saida[2]));
  Flip_Flop_SR flip_flop_sr_3 (
    .S_R(multiplexer_1_out[1]), .Clock(Clock), .Preset(Preset), .Enable(Enable), .Clear(Clear),
    .out_6(valor_saida[1]));
  Multiplexer #(.width(4)) multiplexer_1 (
    .in0(adder_1_out), .in1(valor_retorno), .out(multiplexer_1_out), .sel(comparator_1_eq));  // open: en
  Flip_Flop_SR flip_flop_sr_4 (
    .S_R(multiplexer_1_out[0]), .Clock(Clock), .Preset(Preset), .Enable(Enable), .Clear(Clear),
    .out_6(valor_saida[0]));
  Hex_Digit_Display hex_digit_display_2 (.value(adder_1_out));  // open: dp
  Adder #(.width(4)) adder_1 (.a(valor_saida), .b(4'b0001), .out(adder_1_out));  // open: cin, cout
  Comparator #(.width(4)) comparator_1 (.a(adder_1_out), .b(valor_max__1), .eq(comparator_1_eq));  // open: gt, lt
endmodule

module numero_negativo (
  input  in_1,
  input  in_2,
  input  in_3,
  input  in_4,
  input  in_5,
  input  in_6,
  input  in_7,
  input  in_8
);

  wire [3:0] adder_1_out, adder_2_out, multiplexer_1_out, negator_1_out, not_1_out;

  Adder #(.width(4)) adder_1 (.a({in_1, in_2, in_3, in_4}), .b(4'b0001), .out(adder_1_out));  // open: cin, cout
  Comparator #(.width(4)) comparator_1 (.a(adder_1_out), .b({in_1, in_2, in_3, in_4}));  // open: gt, eq, lt
  Negator #(.width(4)) negator_1 (.in({in_1, in_2, in_3, in_4}), .out(negator_1_out));
  Multiplexer #(.width(4)) multiplexer_1 (
    .in0({in_5, in_6, in_7, in_8}), .in1(adder_2_out), .out(multiplexer_1_out), .sel(in_5));  // open: en
  Hex_Digit_Display hex_digit_display_1 (.value(negator_1_out));  // open: dp
  Hex_Digit_Display hex_digit_display_2 (.value(multiplexer_1_out));  // open: dp
  assign not_1_out = ~{in_5, in_6, in_7, in_8};  // NOT_Gate not_1, 4 bits wide
  Adder #(.width(4)) adder_2 (.a(not_1_out), .b(4'b0001), .out(adder_2_out));  // open: cin, cout
  LED negativo (.in(in_5));
endmodule
